# Fritzing sketch expander-ADS1015-3V3 (saved by Fritzing 0.9.3b)
breadboards: 1

parts:
  Part1 = Arduino Uno (Rev3)
  POT1 = Breadboard Trimpot
  Composant1 = Adafruit ADS1015 12Bit I2C ADC [part_number="Adafruit #1083"]

nets:
  N1: Part1.A4/SDA, Composant1.SDA
  N2: Part1.A5/SCL, Composant1.SCL
  3V3: Part1.3V3, POT1.PIN3, Composant1.VDD
  GND: Part1.GND, POT1.PIN1, Composant1.GND
  N3: POT1.PIN2, Composant1.AIN0

custom parts:
  Adafruit ADS1015 12Bit I2C ADC: For microcontrollers without an analog-to-digital converter or when you want a higher-precision ADC, the ADS1015 provides 12-bit precision at 3300 samples/second over I2C. The chip can be configured as 4 single-ended input channels, or two differential channels. As a nice bonus, it even includes a programmable gain amplifier, up to x16, to help boost up smaller single/differential signals to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
