# Fritzing sketch expander-ADS1015-raspberrypi3 (saved by Fritzing 0.9.3b)
breadboards: 1

parts:
  POT1 = Breadboard Trimpot
  Composant1 = Adafruit ADS1015 12Bit I2C ADC [part_number="Adafruit #1083"]
  Raspberry_Pi_1 = Raspberry Pi 3 [part_number=RPI-3-V1.2]

nets:
  GND: POT1.PIN1, Composant1.GND, Raspberry_Pi_1.GND
  N1: POT1.PIN2, Composant1.AIN0
  VDD: POT1.PIN3, Composant1.VDD, Raspberry_Pi_1.3v3
  N2: Composant1.SDA, Raspberry_Pi_1.GPIO2
  N3: Composant1.SCL, Raspberry_Pi_1.GPIO3

custom parts:
  Adafruit ADS1015 12Bit I2C ADC: For microcontrollers without an analog-to-digital converter or when you want a higher-precision ADC, the ADS1015 provides 12-bit precision at 3300 samples/second over I2C. The chip can be configured as 4 single-ended input channels, or two differential channels. As a nice bonus, it even includes a programmable gain amplifier, up to x16, to help boost up smaller single/differential signals to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
